# Fritzing sketch iotinator (saved by Fritzing 0.9.3b)
breadboards: 2

parts:
  Composant1 = NodeMCU V3.0 0.1"
  Reivaxy1 = OLED 0.96" 128x64 I2C SSD1306 GND First pin
  GSM_SIM_GPSR_SMS_SIM900_SIM1 = SIM800L [package=THT]

nets:
  3V3: Composant1.3V3, Reivaxy1.VCC, GSM_SIM_GPSR_SMS_SIM900_SIM1.5V
  N1: Composant1.GND#6, Composant1.GND#13, Composant1.GND#16, Composant1.GND#33, Reivaxy1.GND, GSM_SIM_GPSR_SMS_SIM900_SIM1.GND#5
  N2: Composant1.D5, Reivaxy1.SCA
  N3: Composant1.D6, Reivaxy1.SCL
  N4: Composant1.D7, GSM_SIM_GPSR_SMS_SIM900_SIM1.SIM_TXD
  N5: Composant1.D8, GSM_SIM_GPSR_SMS_SIM900_SIM1.SIM_RXD

custom parts:
  NodeMCU V3.0 0.1": ESP8266 NodeMCU with 1.1" layout
  OLED 0.96" 128x64 I2C SSD1306 GND First pin: OLED 0.96" 128x64 I2C SSD1306 with GND as first pin
